// Logisim project Curcuit_for_Lab1.circ as structural Verilog: 1 circuit, main circuit main
module main (
  input  Pin_1,
  input  Pin_1_2,
  input  Pin_2,
  input  Pin_2_2,
  input  in_5,
  input  in_6,
  input  Pin_1_3,
  input  Pin_1_4,
  input  Pin_2_3,
  input  Pin_2_4
);

  wire and_1_out, and_2_out, and_3_out, and_4_out, nand_1_out, not_1_out, or_1_out, xor_1_out, xor_2_out,
       xor_3_out;

  and and_1 (and_1_out, Pin_1_2, Pin_2_2);
  not not_1 (not_1_out, in_5);
  xor xor_1 (xor_1_out, Pin_1_4, Pin_2_4);
  and and_2 (and_2_out, Pin_1_4, Pin_2_4);
  LED led_1 (.in(and_1_out));
  LED led_2 (.in(not_1_out));
  LED led_3 (.in(xor_1_out));
  LED led_4 (.in(and_2_out));
  nand nand_1 (nand_1_out, Pin_1, Pin_2);
  xor xor_2 (xor_2_out, Pin_1_3, Pin_2_3);
  and and_3 (and_3_out, Pin_1_3, Pin_2_3);
  LED led_5 (.in(nand_1_out));
  xor xor_3 (xor_3_out, in_6, xor_2_out);
  and and_4 (and_4_out, in_6, xor_2_out);
  or or_1 (or_1_out, and_4_out, and_3_out);
  LED led_6 (.in(xor_3_out));
  LED led_7 (.in(or_1_out));

  // Notes on the sheet:
  //   AND GATE
  //   NOT GATE
  //   Sum
  //   Carry
  //   NAND Gate
endmodule
