// Logisim project Curcuit_for_Lab2.circ as structural Verilog: 1 circuit, main circuit main
module main (
  input  in_1,
  input  Pin_1,
  input  B0,
  input  Pin_2,
  input  in_5,
  input  B1,
  input  Pin_3,
  input  Pin_4,
  input  Pin_1_2,
  input  in_10,
  input  Pin_2_2,
  input  B2,
  input  in_13,
  input  B3
);

  wire and_1_out, and_2_out, and_3_out, and_4_out, and_5_out, and_6_out, and_7_out, and_8_out, and_9_out,
       and_10_out, and_11_out, or_1_out, or_2_out, or_3_out, or_4_out, xor_1_out, xor_2_out, xor_3_out,
       xor_4_out, xor_5_out, xor_6_out, xor_7_out, xor_8_out, xor_9_out, xor_10_out, xor_11_out;

  xor xor_1 (xor_1_out, Pin_1_2, Pin_2_2);
  and and_1 (and_1_out, Pin_1_2, Pin_2_2);
  LED led_1 (.in(xor_1_out));
  LED led_2 (.in(and_1_out));
  and and_2 (and_2_out, Pin_1, Pin_2);
  xor xor_2 (xor_2_out, Pin_3, Pin_4);
  xor xor_3 (xor_3_out, Pin_1, Pin_2);
  xor xor_4 (xor_4_out, and_2_out, xor_2_out);
  and and_3 (and_3_out, and_2_out, xor_2_out);
  and and_4 (and_4_out, Pin_3, Pin_4);
  LED led_3 (.in(xor_3_out));
  or or_1 (or_1_out, and_3_out, and_4_out);
  LED led_4 (.in(and_2_out));
  LED led_5 (.in(xor_4_out));
  LED led_6 (.in(or_1_out));
  xor xor_5 (xor_5_out, in_1, B0);
  and and_5 (and_5_out, in_1, B0);
  xor xor_6 (xor_6_out, in_5, B1);
  xor xor_7 (xor_7_out, in_10, B2);
  xor xor_8 (xor_8_out, in_13, B3);
  xor xor_9 (xor_9_out, and_5_out, xor_6_out);
  and and_6 (and_6_out, and_5_out, xor_6_out);
  and and_7 (and_7_out, in_5, B1);
  LED led_7 (.in(xor_5_out));
  LED led_8 (.in(and_5_out));
  xor xor_10 (xor_10_out, or_2_out, xor_7_out);
  and and_8 (and_8_out, or_2_out, xor_7_out);
  and and_9 (and_9_out, in_10, B2);
  xor xor_11 (xor_11_out, or_3_out, xor_8_out);
  and and_10 (and_10_out, or_3_out, xor_8_out);
  and and_11 (and_11_out, in_13, B3);
  LED led_9 (.in(xor_9_out));
  or or_2 (or_2_out, and_6_out, and_7_out);
  LED led_10 (.in(or_2_out));
  LED led_11 (.in(xor_10_out));
  or or_3 (or_3_out, and_8_out, and_9_out);
  LED led_12 (.in(or_3_out));
  LED led_13 (.in(xor_11_out));
  buf or_4 (or_4_out, and_11_out);  // OR_Gate
  LED led_14 (.in(or_4_out));

  // Notes on the sheet:
  //   Half Adder
  //   Sum
  //   Carry
  //   FULL ADDER
  //   Sum0
  //   Carry0 
  //   Sum1
  //   Carry1
  //   A0
  //   A1
  //   A2
  //   A3
  //   S0
  //   Cout0
  //   S1
  //   Cout1
  //   S2
  //   S3
  //   Cout2
  //   Cout3
endmodule
