// Logisim project Circuit_for_lab3.circ as structural Verilog: 1 circuit, main circuit main
module main (
  input  Set,
  input  J,
  input  K,
  input  Reset,
  input  in_5,
  input  in_6,
  input  in_7,
  input  in_8,
  input  in_9
);

  wire and_1_out, and_2_out, and_3_out, and_4_out, clock_1_out, clock_2_out, clock_3_out, d_ff_1_q,
       d_ff_1_qn, d_ff_2_q, d_ff_2_qn, d_ff_3_q, d_ff_3_qn, d_ff_4_q, d_ff_4_qn, nand_1_out, nand_2_out,
       nor_1_out, nor_2_out, nor_3_out, nor_4_out, not_1_out;

  Clock clock_1 (.out(clock_1_out));
  not not_1 (not_1_out, in_9);
  nor nor_1 (nor_1_out, Set, nor_2_out);
  nor nor_2 (nor_2_out, nor_1_out, Reset);
  LED led_1 (.in(nor_1_out));
  LED led_2 (.in(nor_2_out));
  and and_1 (and_1_out, not_1_out, clock_1_out);
  and and_2 (and_2_out, clock_1_out, in_9);
  nor nor_3 (nor_3_out, and_1_out, nor_4_out);
  nor nor_4 (nor_4_out, nor_3_out, and_2_out);
  LED led_3 (.in(nor_3_out));
  LED led_4 (.in(nor_4_out));
  Clock clock_2 (.out(clock_2_out));
  Clock clock_3 (.out(clock_3_out));
  D_Flip_Flop d_ff_1 (.D(in_5), .clk(clock_3_out), .Q(d_ff_1_q), .Qn(d_ff_1_qn));  // open: preset, reset
  LED led_5 (.in(d_ff_1_q));
  LED led_6 (.in(d_ff_1_qn));
  and and_3 (and_3_out, nand_2_out, clock_2_out);
  and and_4 (and_4_out, clock_2_out, nand_1_out);
  D_Flip_Flop d_ff_2 (.D(in_6), .clk(clock_3_out), .Q(d_ff_2_q), .Qn(d_ff_2_qn));  // open: preset, reset
  LED led_7 (.in(d_ff_2_q));
  LED led_8 (.in(d_ff_2_qn));
  // AND_Gate and_5 has open pins: in0=and_3_out, in1=nand_2_out, out=open
  nand nand_1 (nand_1_out, and_3_out, nand_2_out);
  nand nand_2 (nand_2_out, nand_1_out, and_4_out);
  D_Flip_Flop d_ff_3 (.D(in_7), .clk(clock_3_out), .Q(d_ff_3_q), .Qn(d_ff_3_qn));  // open: preset, reset
  LED led_9 (.in(d_ff_3_q));
  LED led_10 (.in(d_ff_3_qn));
  LED led_11 (.in(nand_1_out));
  LED led_12 (.in(nand_2_out));
  D_Flip_Flop d_ff_4 (.D(in_8), .clk(clock_3_out), .Q(d_ff_4_q), .Qn(d_ff_4_qn));  // open: preset, reset
  LED led_13 (.in(d_ff_4_q));
  LED led_14 (.in(d_ff_4_qn));

  // Notes on the sheet:
  //   0
  //   D Flip Flop
  //   R-S Flip Flop using pair of input NOR gates
  //   1
  //   Q
  //   Q'
  //   Q
  //   Q'
  //   J-K Flip Flops
  //   Register
  //   Q
  //   Q'
endmodule
