// Logisim project Circuit_of_lab4.circ as structural Verilog: 1 circuit, main circuit main
module main (
  input  in_1,
  input  in_2,
  input  in_3,
  input  in_4,
  input  in_5
);

  wire and_1_out, and_2_out, clock_1_out, clock_2_out, clock_3_out, clock_4_out, j_k_ff_1_q, j_k_ff_2_q,
       j_k_ff_3_q, j_k_ff_4_q, j_k_ff_5_q, j_k_ff_6_q, j_k_ff_7_q, j_k_ff_8_q, j_k_ff_9_q, j_k_ff_10_q,
       j_k_ff_11_q, j_k_ff_12_q;
  wire [2:0] d_ff_1_q;

  Clock clock_1 (.out(clock_1_out));
  Clock clock_2 (.out(clock_2_out));
  J_K_Flip_Flop j_k_ff_1 (.J(in_1), .K(in_1), .clk(clock_1_out), .Q(j_k_ff_1_q));  // open: Qn, preset, reset
  J_K_Flip_Flop j_k_ff_2 (.J(in_4), .K(in_4), .clk(clock_2_out), .Q(j_k_ff_2_q));  // open: Qn, preset, reset
  LED led_1 (.in(j_k_ff_1_q));
  LED led_2 (.in(j_k_ff_2_q));
  J_K_Flip_Flop j_k_ff_3 (.J(in_1), .K(in_1), .clk(j_k_ff_1_q), .Q(j_k_ff_3_q));  // open: Qn, preset, reset
  J_K_Flip_Flop j_k_ff_4 (.J(in_4), .K(in_4), .clk(j_k_ff_2_q), .Q(j_k_ff_4_q));  // open: Qn, preset, reset
  LED led_3 (.in(j_k_ff_3_q));
  LED led_4 (.in(j_k_ff_4_q));
  J_K_Flip_Flop j_k_ff_5 (.J(in_1), .K(in_1), .clk(j_k_ff_3_q), .Q(j_k_ff_5_q));  // open: Qn, preset, reset
  J_K_Flip_Flop j_k_ff_6 (.J(in_4), .K(in_4), .clk(j_k_ff_4_q), .Q(j_k_ff_6_q));  // open: Qn, preset, reset
  LED led_5 (.in(j_k_ff_5_q));
  LED led_6 (.in(j_k_ff_6_q));
  Clock clock_3 (.out(clock_3_out));
  J_K_Flip_Flop j_k_ff_7 (
    .J(in_2), .K(in_2), .clk(clock_3_out), .Q(j_k_ff_7_q), .reset(and_1_out));  // open: Qn, preset
  LED led_7 (.in(j_k_ff_7_q));
  J_K_Flip_Flop j_k_ff_8 (.J(in_2), .K(in_2), .clk(j_k_ff_7_q), .Q(j_k_ff_8_q), .reset(and_1_out));  // open: Qn, preset
  LED led_8 (.in(j_k_ff_8_q));
  and and_1 (and_1_out, j_k_ff_8_q, j_k_ff_9_q);
  J_K_Flip_Flop j_k_ff_9 (.J(in_2), .K(in_2), .clk(j_k_ff_8_q), .Q(j_k_ff_9_q), .reset(and_1_out));  // open: Qn, preset
  LED led_9 (.in(j_k_ff_9_q));
  Clock clock_4 (.out(clock_4_out));
  J_K_Flip_Flop j_k_ff_10 (.J(in_3), .K(in_3), .clk(clock_4_out), .Q(j_k_ff_10_q));  // open: Qn, preset, reset
  LED led_10 (.in(j_k_ff_10_q));
  J_K_Flip_Flop j_k_ff_11 (
    .J(in_3), .K(in_3), .clk(j_k_ff_10_q), .Q(j_k_ff_11_q), .reset(and_2_out));  // open: Qn, preset
  D_Flip_Flop d_ff_1 (.D(j_k_ff_10_q), .clk(clock_4_out), .Q(d_ff_1_q[0]));  // open: Qn, preset, reset
  LED led_11 (.in(j_k_ff_11_q));
  D_Flip_Flop d_ff_2 (.D(j_k_ff_11_q), .clk(clock_4_out), .Q(d_ff_1_q[1]));  // open: Qn, preset, reset
  J_K_Flip_Flop j_k_ff_12 (
    .J(in_3), .K(in_3), .clk(j_k_ff_11_q), .Q(j_k_ff_12_q), .reset(and_2_out));  // open: Qn, preset
  and and_2 (and_2_out, j_k_ff_11_q, j_k_ff_12_q);
  LED led_12 (.in(j_k_ff_12_q));
  D_Flip_Flop d_ff_3 (.D(j_k_ff_12_q), .clk(clock_4_out), .Q(d_ff_1_q[2]));  // open: Qn, preset, reset
  Hex_Digit_Display hex_digit_display_1 (.value({in_5, d_ff_1_q}));  // open: dp

  // Notes on the sheet:
  //   Least Significant
  //   JK Flip Flops UP
  //   JK Flip Flops DOWN
  //   Q0
  //   Q0
  //   Q1
  //   Q1
  //   Q2
  //   Q2
  //   Most Significant
  //   Least Significant
  //   Q0
  //   Q1
  //   Q2
  //   Most Significant
  //   Q0
  //   1
  //   Q1
  //   Q2
  //   Most Significant
  //   4
endmodule
