// Logisim project Circuit_for_lab5.circ as structural Verilog: 1 circuit, main circuit main
module main (
  input  in_1,
  input  in_2,
  input  in_3,
  input  LeftRight,
  input  in_5,
  input  in_6,
  input  Trigger
);

  wire and_1_out, and_2_out, and_3_out, and_4_out, and_5_out, and_6_out, and_7_out, and_8_out, and_9_out,
       and_10_out, and_11_out, and_12_out, and_13_out, and_14_out, and_15_out, and_16_out, and_17_out,
       and_18_out, and_19_out, and_20_out, button_1_out, clock_1_out, clock_2_out, d_ff_1_q, d_ff_2_q,
       d_ff_3_q, d_ff_4_q, d_ff_5_q, d_ff_6_q, d_ff_7_q, d_ff_8_q, d_ff_9_q, d_ff_10_q, d_ff_11_q, d_ff_12_q,
       d_ff_13_q, d_ff_14_q, d_ff_15_q, not_1_out, not_2_out, or_1_out, or_2_out, or_3_out, or_4_out,
       or_5_out, or_6_out, or_7_out, or_8_out, or_9_out, or_10_out;

  Button button_1 (.out(button_1_out));
  and and_1 (and_1_out, in_1, in_3);
  Clock clock_1 (.out(clock_1_out));
  not not_1 (not_1_out, LeftRight);
  and and_2 (and_2_out, LeftRight, in_6);
  and and_3 (and_3_out, not_1_out, d_ff_4_q);
  or or_1 (or_1_out, and_2_out, and_3_out);
  Clock clock_2 (.out(clock_2_out));
  not not_2 (not_2_out, in_1);
  and and_4 (and_4_out, not_2_out, d_ff_5_q);
  or or_2 (or_2_out, and_1_out, and_4_out);
  D_Flip_Flop d_ff_1 (.D(or_2_out), .clk(clock_1_out), .Q(d_ff_1_q));  // open: Qn, preset, reset
  D_Flip_Flop d_ff_2 (.D(or_1_out), .clk(clock_2_out), .Q(d_ff_2_q), .reset(button_1_out));  // open: Qn, preset
  LED led_1 (.in(d_ff_2_q));
  LED led_2 (.in(d_ff_1_q));
  and and_5 (and_5_out, LeftRight, d_ff_2_q);
  D_Flip_Flop d_ff_3 (.D(d_ff_2_q), .clk(Trigger), .Q(d_ff_3_q), .reset(button_1_out));  // open: Qn, preset
  and and_6 (and_6_out, in_1, d_ff_1_q);
  or or_3 (or_3_out, and_6_out, and_8_out);
  and and_7 (and_7_out, not_1_out, d_ff_7_q);
  or or_4 (or_4_out, and_5_out, and_7_out);
  D_Flip_Flop d_ff_4 (.D(or_4_out), .clk(clock_2_out), .Q(d_ff_4_q), .reset(button_1_out));  // open: Qn, preset
  LED led_3 (.in(d_ff_3_q));
  and and_8 (and_8_out, not_2_out, d_ff_8_q);
  D_Flip_Flop d_ff_5 (.D(or_3_out), .clk(clock_1_out), .Q(d_ff_5_q));  // open: Qn, preset, reset
  LED led_4 (.in(d_ff_5_q));
  LED led_5 (.in(d_ff_4_q));
  D_Flip_Flop d_ff_6 (.D(d_ff_4_q), .clk(Trigger), .Q(d_ff_6_q), .reset(button_1_out));  // open: Qn, preset
  and and_9 (and_9_out, LeftRight, d_ff_4_q);
  or or_5 (or_5_out, and_9_out, and_12_out);
  D_Flip_Flop d_ff_7 (.D(or_5_out), .clk(clock_2_out), .Q(d_ff_7_q), .reset(button_1_out));  // open: Qn, preset
  LED led_6 (.in(d_ff_6_q));
  and and_10 (and_10_out, in_1, d_ff_5_q);
  and and_11 (and_11_out, not_2_out, d_ff_11_q);
  or or_6 (or_6_out, and_10_out, and_11_out);
  D_Flip_Flop d_ff_8 (.D(or_6_out), .clk(clock_1_out), .Q(d_ff_8_q));  // open: Qn, preset, reset
  and and_12 (and_12_out, not_1_out, d_ff_10_q);
  LED led_7 (.in(d_ff_7_q));
  LED led_8 (.in(d_ff_8_q));
  and and_13 (and_13_out, LeftRight, d_ff_7_q);
  D_Flip_Flop d_ff_9 (.D(d_ff_7_q), .clk(Trigger), .Q(d_ff_9_q), .reset(button_1_out));  // open: Qn, preset
  and and_14 (and_14_out, in_1, d_ff_8_q);
  or or_7 (or_7_out, and_14_out, and_16_out);
  and and_15 (and_15_out, not_1_out, d_ff_13_q);
  or or_8 (or_8_out, and_13_out, and_15_out);
  D_Flip_Flop d_ff_10 (.D(or_8_out), .clk(clock_2_out), .Q(d_ff_10_q), .reset(button_1_out));  // open: Qn, preset
  LED led_9 (.in(d_ff_9_q));
  and and_16 (and_16_out, not_2_out, d_ff_14_q);
  D_Flip_Flop d_ff_11 (.D(or_7_out), .clk(clock_1_out), .Q(d_ff_11_q));  // open: Qn, preset, reset
  LED led_10 (.in(d_ff_10_q));
  LED led_11 (.in(d_ff_11_q));
  and and_17 (and_17_out, LeftRight, d_ff_10_q);
  D_Flip_Flop d_ff_12 (.D(d_ff_10_q), .clk(Trigger), .Q(d_ff_12_q), .reset(button_1_out));  // open: Qn, preset
  LED led_12 (.in(d_ff_12_q));
  and and_18 (and_18_out, in_1, d_ff_11_q);
  or or_9 (or_9_out, and_18_out, and_20_out);
  and and_19 (and_19_out, not_1_out, in_5);
  or or_10 (or_10_out, and_17_out, and_19_out);
  D_Flip_Flop d_ff_13 (.D(or_10_out), .clk(clock_2_out), .Q(d_ff_13_q), .reset(button_1_out));  // open: Qn, preset
  and and_20 (and_20_out, not_2_out, in_2);
  D_Flip_Flop d_ff_14 (.D(or_9_out), .clk(clock_1_out), .Q(d_ff_14_q));  // open: Qn, preset, reset
  LED led_13 (.in(d_ff_13_q));
  D_Flip_Flop d_ff_15 (.D(d_ff_13_q), .clk(Trigger), .Q(d_ff_15_q), .reset(button_1_out));  // open: Qn, preset
  LED led_14 (.in(d_ff_14_q));
  LED led_15 (.in(d_ff_15_q));

  // Notes on the sheet:
  //   Reset
  //   5 bit deep , 1 bit wide stack
endmodule
